# Fritzing sketch BattyMeter_schematic (saved by Fritzing 0.9.3b)

parts:
  Part1 = Arduino Nano (Rev3.0)
  ACS712_Current_Sensor1 = ACS712 Current Sensor
  ACS712_Current_Sensor2 = ACS712 Current Sensor
  J2 = Screw terminal - 2 pins [package=THT]
  microSD1 = MicroSD Card Module
  R1 = Resistor [tolerance=±5% resistance=10k package=THT]
  R2 = Resistor [tolerance=±5% resistance=100k package=THT]
  J3 = Screw terminal - 2 pins [package=THT]
  R3 = Resistor [tolerance=±5% resistance=10k package=THT]
  R4 = Resistor [tolerance=±5% resistance=100k package=THT]
  R5 = Resistor [tolerance=±5% resistance=1k package=THT]
  LCD1 = LCD screen

nets:
  GND: Part1.GND, ACS712_Current_Sensor2.GND, LCD1.R/W
  N1: Part1.D4, microSD1.CS
  N2: Part1.D5, LCD1.DB7
  N3: Part1.D6, LCD1.DB6
  N4: Part1.D7, LCD1.DB5
  N5: Part1.D8, LCD1.DB4
  N6: Part1.D9, LCD1.E
  N7: Part1.D10, LCD1.RS
  N8: Part1.D11/MOSI, microSD1.MOSI
  N9: Part1.D12/MISO, microSD1.MISO
  5V: Part1.5V, LCD1.VDD
  N10: Part1.A3, R3.Pin_1, R4.Pin_1
  N11: Part1.A2, ACS712_Current_Sensor1.OUT
  N12: Part1.A1, ACS712_Current_Sensor2.OUT
  N13: Part1.A0, R1.Pin_1, R2.Pin_1
  N14: Part1.D13/SCK, microSD1.SCK
  N15: J2.pin1, R1.Pin_0
  N16: J2.pin2, R2.Pin_0
  GND_2: microSD1.GND, R5.Pin_0, LCD1.VSS
  N17: J3.pin1, R3.Pin_0
  N18: J3.pin2, R4.Pin_0
  N19: R5.Pin_1, LCD1.V0

custom parts:
  ACS712 Current Sensor: A breakout board for the Allegro ACS712 is a Hall Effect-based linear current sensor. The module operates at 5V.
